# Fritzing sketch Prueba en Fritzing (saved by Fritzing 0.6.3b)
breadboards: 1

parts:
  Arduino1 = Arduino
  U1 = Barometric Pressure Sensor
  U2 = 3-Axis Accelerometer Breakout
  U3 = XBee

nets:
  GND: Arduino1.GND, U1.GND, U3.GND
  N1: Arduino1.D13, U1.SCK
  N2: Arduino1.D12, U1.MISO
  N3: Arduino1.D11, U1.MOSI
  N4: Arduino1.D7, U1.CSB
  N5: Arduino1.D6, U1.DRDY
  N6: Arduino1.D1TX, U3.pin3
  N7: Arduino1.D0RX, U3.pin2
  3V3: Arduino1.3V3, U1.3.3V
  +5V: Arduino1.+5V, U3.VCC
  N8: Arduino1.A0, U2.ST
  N9: Arduino1.A1, U2.Z
  N10: Arduino1.A2, U2.Y
  N11: Arduino1.A3, U2.X
  N12: Arduino1.A4, U2.GND
  N13: Arduino1.A5, U2.VDD

notes:
  IZM
  Carga útil de CanSat. v.1
  Israel Zuñiga de la Mora
